// Logisim project 2011_2021.circ as structural Verilog: 2 circuits, main circuit 状态转移
module \状态转移  (
  input  S2,
  input  S1,
  input  S0,
  input  IN1,
  input  IN0,
  output S22,
  output S11,
  output S00,
  output OUT1,
  output OUT0
);

  wire and_1_out, and_2_out, and_5_out, and_6_out, and_7_out, and_8_out, and_9_out, and_10_out, and_11_out,
       not_1_out, not_2_out, not_3_out, not_4_out, not_5_out, not_6_out, not_7_out, not_8_out, not_9_out;

  not not_1 (not_1_out, S0);
  not not_2 (not_2_out, S1);
  not not_3 (not_3_out, IN1);
  not not_4 (not_4_out, IN0);
  not not_5 (not_5_out, S0);
  not not_6 (not_6_out, IN1);
  not not_7 (not_7_out, IN0);
  not not_8 (not_8_out, S1);
  not not_9 (not_9_out, S0);
  and and_1 (and_1_out, S2, IN0);
  and and_2 (and_2_out, S2, S1);
  and and_3 (OUT0, S1, S0, IN0);
  and and_4 (S22, S1, not_1_out, IN1);
  and and_5 (and_5_out, not_2_out, S0, not_3_out, not_4_out);
  and and_6 (and_6_out, S1, not_5_out, IN0);
  and and_7 (and_7_out, S2, not_6_out, not_7_out);
  and and_8 (and_8_out, S2, S1);
  and and_9 (and_9_out, not_8_out, IN1);
  and and_10 (and_10_out, S1, not_9_out, IN0);
  and and_11 (and_11_out, S2, S1);
  or or_1 (OUT1, and_1_out, and_2_out);
  or or_2 (S11, and_5_out, and_6_out, and_7_out, and_8_out);
  or or_3 (S00, and_9_out, and_10_out, and_11_out);
endmodule

module \状态存储  (
  input  [1:0] in_1,
  output [1:0] out_2
);

  wire CLK, S0, S00, S1, S2, S11, S22;

  Clock clock_1 (.out(CLK));
  Register #(.width(1)) u_s2 (.D(S22), .Q(S2), .clk(CLK));  // open: en, clr
  Register #(.width(1)) u_s1 (.D(S11), .Q(S1), .clk(CLK));  // open: en, clr
  \状态转移  \u_状态转移_1  (
    .S2(S2), .S1(S1), .S0(S0), .IN1(in_1[1]), .IN0(in_1[0]), .S22(S22), .S11(S11), .S00(S00),
    .OUT1(out_2[1]), .OUT0(out_2[0]));
  Register #(.width(1)) u_s0 (.D(S00), .Q(S0), .clk(CLK));  // open: en, clr

  // Other names for the same wires on the sheet: IN0 = in_1[0]; IN1 = in_1[1]; OUT0 = out_2[0]; OUT1 = out_2[1]

  // Notes on the sheet:
  //   设计一个Mealy型电路，若序列的一个后缀为字符串2011，则输出1；如果为2021，则输出2，其他情况都输出0。
endmodule
