// Logisim project CRC.circ as structural Verilog: 2 circuits, main circuit CRC
module CRC (
  input  [3:0] B,
  input  [7:0] A,
  output [10:0] C
);

  wire [2:0] n4_bit_1_a_b, n4_bit_2_a_b, n4_bit_3_a_b, n4_bit_4_a_b, n4_bit_5_a_b, n4_bit_6_a_b;
  wire [3:1] n4_bit_7_a_b;

  _4_bit u_4_bit_1 (.b(B), .a(A[7:4]), .a_b(n4_bit_1_a_b));  // open: a_b_2
  _4_bit u_4_bit_2 (.b(B), .a({n4_bit_1_a_b, A[3]}), .a_b(n4_bit_2_a_b));  // open: a_b_2
  _4_bit u_4_bit_3 (.b(B), .a({n4_bit_2_a_b, A[2]}), .a_b(n4_bit_3_a_b));  // open: a_b_2
  _4_bit u_4_bit_4 (.b(B), .a({n4_bit_3_a_b, A[1]}), .a_b(n4_bit_4_a_b));  // open: a_b_2
  _4_bit u_4_bit_5 (.b(B), .a({n4_bit_4_a_b, A[0]}), .a_b(n4_bit_5_a_b));  // open: a_b_2
  _4_bit u_4_bit_6 (.b(B), .a({n4_bit_5_a_b, 1'b0}), .a_b(n4_bit_6_a_b));  // open: a_b_2
  _4_bit u_4_bit_7 (.b(B), .a({n4_bit_6_a_b, 1'b0}), .a_b(n4_bit_7_a_b));  // open: a_b_2
  _4_bit u_4_bit_8 (.b(B), .a({n4_bit_7_a_b, 1'b0}), .a_b(C[2:0]));  // open: a_b_2

  assign C[10:3] = A;

  // Other names for the same wires on the sheet: yushu[2:0] = C[2:0]
endmodule

module _4_bit (
  input  [3:0] b,
  input  [3:0] a,
  output [2:0] a_b,
  output a_b_2
);

  wire [2:0] xor_1_out;

  assign xor_1_out = b[2:0] ^ a[2:0];  // XOR_Gate xor_1, 3 bits wide
  Multiplexer #(.width(3)) multiplexer_1 (.in0(a[2:0]), .in1(xor_1_out), .out(a_b), .sel(a[3]));  // open: en

  assign a_b_2 = a[3];

  // Notes on the sheet:
  //   a/b
endmodule
