// Logisim project GRF.circ as structural Verilog: 4 circuits, main circuit grf
module grf (
  input  CLK,
  input  RESET,
  input  WE,
  input  [4:0] A1,
  input  [4:0] A2,
  input  [4:0] A3,
  input  [31:0] WD,
  output [31:0] RD1,
  output [31:0] RD2
);

  Clock clock_1 ();  // open: out
  _32_registers u_32_registers_1 (
    .WD(WD), .A1(A1), .A2(A2), .A3(A3), .CLK(CLK), .WE(WE), .CLR(RESET), .RD1(RD1), .RD2(RD2));
endmodule

module _32_registers (
  input  [31:0] WD,
  input  [4:0] A1,
  input  [4:0] A2,
  input  [4:0] A3,
  input  CLK,
  input  WE,
  input  CLR,
  output [31:0] RD1,
  output [31:0] RD2
);

  wire _00, _11, _22, _33, and_1_out, and_2_out, and_3_out, and_4_out;
  wire [31:0] _0, _1, _2, _3, RD01, RD02, RD11, RD12, RD21, RD22, RD31, RD32;

  Demultiplexer #(.select(2), .width(32), .disabled(0), .enable("false")) demultiplexer_1 (
    .out0(_0), .out1(_1), .out2(_2), .out3(_3), .in(WD), .sel(A3[4:3]));
  and and_1 (and_1_out, WE, _22);
  and and_2 (and_2_out, WE, _00);
  _8_rigisters u_8_rigisters_1 (
    .WD(_2), .A3(A3[2:0]), .WE(and_1_out), .CLK(CLK), .CLR(CLR), .A1(A1[2:0]), .A2(A2[2:0]), .RD1(RD21),
    .RD2(RD22));
  Decoder #(.select(2)) decoder_1 (.out0(_00), .out1(_11), .out2(_22), .out3(_33), .sel(A3[4:3]));  // open: en
  _8_rigister_1 u_8_rigister_1_1 (
    .WD(_0), .RD1(RD01), .A1(A1[2:0]), .A3(A3[2:0]), .WE(and_2_out), .RD2(RD02), .CLK(CLK), .CLR(CLR),
    .A2(A2[2:0]));
  and and_3 (and_3_out, WE, _33);
  and and_4 (and_4_out, WE, _11);
  _8_rigisters u_8_rigisters_2 (
    .WD(_3), .A3(A3[2:0]), .WE(and_3_out), .CLK(CLK), .CLR(CLR), .A1(A1[2:0]), .A2(A2[2:0]), .RD1(RD31),
    .RD2(RD32));
  _8_rigisters u_8_rigisters_3 (
    .WD(_1), .A3(A3[2:0]), .WE(and_4_out), .CLK(CLK), .CLR(CLR), .A1(A1[2:0]), .A2(A2[2:0]), .RD1(RD11),
    .RD2(RD12));
  Multiplexer #(.select(2), .width(32)) multiplexer_1 (
    .in0(RD02), .in1(RD12), .in2(RD22), .in3(RD32), .out(RD2), .sel(A2[4:3]));  // open: en
  Multiplexer #(.select(2), .width(32)) multiplexer_2 (
    .in0(RD01), .in1(RD11), .in2(RD21), .in3(RD31), .out(RD1), .sel(A1[4:3]));  // open: en

  // Other names for the same wires on the sheet: A1M[2:0] = A1[2:0]; A1C[1:0] = A1[4:3]; A2M[2:0] = A2[2:0];
  //   A2C[1:0] = A2[4:3]; A3M[2:0] = A3[2:0]; A3C[1:0] = A3[4:3]
endmodule

module _8_rigisters (
  input  [31:0] WD,
  input  [2:0] A1,
  input  [2:0] A3,
  input  WE,
  input  CLK,
  input  CLR,
  input  [2:0] A2,
  output [31:0] RD1,
  output [31:0] RD2
);

  wire W0, W00, W01, W1, W02, W2, W03, W3, W04, W4, W05, W5, W06, W6, W07, W7;
  wire [31:0] _0, _0i, _1, _1i, _2, _2i, _3, _3i, _4, _4i, _5, _5i, _6, _6i, _7, _7i;

  Demultiplexer #(.select(3), .width(32), .enable("false")) demultiplexer_1 (
    .out0(_0i), .out1(_1i), .out2(_2i), .out3(_3i), .out4(_4i), .out5(_5i), .out6(_6i), .out7(_7i), .in(WD),
    .sel(A3));
  Decoder #(.select(3), .enable("false")) decoder_1 (
    .out0(W0), .out1(W1), .out2(W2), .out3(W3), .out4(W4), .out5(W5), .out6(W6), .out7(W7), .sel(A3));
  Register #(.width(32)) register_1 (.D(_0i), .en(W00), .Q(_0), .clk(CLK), .clr(CLR));
  Register #(.width(32)) register_2 (.D(_1i), .en(W01), .Q(_1), .clk(CLK), .clr(CLR));
  Register #(.width(32)) register_3 (.D(_2i), .en(W02), .Q(_2), .clk(CLK), .clr(CLR));
  Register #(.width(32)) register_4 (.D(_3i), .en(W03), .Q(_3), .clk(CLK), .clr(CLR));
  and and_1 (W00, W0, WE);
  and and_2 (W01, WE, W1);
  and and_3 (W02, WE, W2);
  and and_4 (W03, WE, W3);
  and and_5 (W04, WE, W4);
  and and_6 (W05, WE, W5);
  Register #(.width(32)) register_5 (.D(_4i), .en(W04), .Q(_4), .clk(CLK), .clr(CLR));
  Register #(.width(32)) register_6 (.D(_5i), .en(W05), .Q(_5), .clk(CLK), .clr(CLR));
  Register #(.width(32)) register_7 (.D(_6i), .en(W06), .Q(_6), .clk(CLK), .clr(CLR));
  Register #(.width(32)) register_8 (.D(_7i), .en(W07), .Q(_7), .clk(CLK), .clr(CLR));
  and and_7 (W06, WE, W6);
  and and_8 (W07, WE, W7);
  Multiplexer #(.select(3), .width(32)) multiplexer_1 (
    .in0(_0), .in1(_1), .in2(_2), .in3(_3), .in4(_4), .in5(_5), .in6(_6), .in7(_7), .out(RD1), .sel(A1));  // open: en
  Multiplexer #(.select(3), .width(32)) multiplexer_2 (
    .in0(_0), .in1(_1), .in2(_2), .in3(_3), .in4(_4), .in5(_5), .in6(_6), .in7(_7), .out(RD2), .sel(A2));  // open: en
endmodule

module _8_rigister_1 (
  input  [31:0] WD,
  input  [2:0] A1,
  input  [2:0] A3,
  input  WE,
  input  CLK,
  input  CLR,
  input  [2:0] A2,
  output [31:0] RD1,
  output [31:0] RD2
);

  wire W0, W00, W01, W1, W02, W2, W03, W3, W04, W4, W05, W5, W06, W6, W07, W7;
  wire [31:0] _0, _0i, _1, _1i, _2, _2i, _3, _3i, _4, _4i, _5, _5i, _6, _6i, _7, _7i;

  Demultiplexer #(.select(3), .width(32), .enable("false")) demultiplexer_1 (
    .out0(_0i), .out1(_1i), .out2(_2i), .out3(_3i), .out4(_4i), .out5(_5i), .out6(_6i), .out7(_7i), .in(WD),
    .sel(A3));
  Decoder #(.select(3), .enable("false")) decoder_1 (
    .out0(W0), .out1(W1), .out2(W2), .out3(W3), .out4(W4), .out5(W5), .out6(W6), .out7(W7), .sel(A3));
  Register #(.width(32)) register_1 (.D({32{1'b0}}), .en(W00), .Q(_0), .clk(CLK), .clr(CLR));
  Register #(.width(32)) register_2 (.D(_1i), .en(W01), .Q(_1), .clk(CLK), .clr(CLR));
  Register #(.width(32)) register_3 (.D(_2i), .en(W02), .Q(_2), .clk(CLK), .clr(CLR));
  Register #(.width(32)) register_4 (.D(_3i), .en(W03), .Q(_3), .clk(CLK), .clr(CLR));
  and and_1 (W00, W0, WE);
  and and_2 (W01, WE, W1);
  and and_3 (W02, WE, W2);
  and and_4 (W03, WE, W3);
  and and_5 (W04, WE, W4);
  and and_6 (W05, WE, W5);
  Register #(.width(32)) register_5 (.D(_4i), .en(W04), .Q(_4), .clk(CLK), .clr(CLR));
  Register #(.width(32)) register_6 (.D(_5i), .en(W05), .Q(_5), .clk(CLK), .clr(CLR));
  Register #(.width(32)) register_7 (.D(_6i), .en(W06), .Q(_6), .clk(CLK), .clr(CLR));
  Register #(.width(32)) register_8 (.D(_7i), .en(W07), .Q(_7), .clk(CLK), .clr(CLR));
  and and_7 (W06, WE, W6);
  and and_8 (W07, WE, W7);
  Multiplexer #(.select(3), .width(32)) multiplexer_1 (
    .in0(_0), .in1(_1), .in2(_2), .in3(_3), .in4(_4), .in5(_5), .in6(_6), .in7(_7), .out(RD1), .sel(A1));  // open: en
  Multiplexer #(.select(3), .width(32)) multiplexer_2 (
    .in0(_0), .in1(_1), .in2(_2), .in3(_3), .in4(_4), .in5(_5), .in6(_6), .in7(_7), .out(RD2), .sel(A2));  // open: en
endmodule
