// Logisim project fsm.circ as structural Verilog: 4 circuits, main circuit fsm
module fsm (
  input  reset,
  input  [1:0] in,
  output z
);

  \输出  \u_输出_1  (.reset(reset), .in(in), .z(z));
endmodule

module \输出  (
  input  reset,
  input  [1:0] in,
  output z
);

  wire CLK, S0, S00, S1, S11;

  Clock u_clk (.out(CLK));
  // Probe on S1
  \置位清零  u_s1 (.D(S11), .Q(S1), .CLK(CLK), .RESET(reset));
  // Probe on S0
  \置位清零  u_s0 (.D(S00), .Q(S0), .CLK(CLK), .RESET(reset));
  \状态转移  \u_状态转移_1  (.S1(S1), .S0(S0), .IN1(in[1]), .IN0(in[0]), .S11(S11), .S00(S00), .Z(z));
endmodule

module \状态转移  (
  input  S1,
  input  S0,
  input  IN1,
  input  IN0,
  output S11,
  output S00,
  output Z
);

  wire and_2_out, and_3_out, not_1_out, not_2_out, not_3_out, not_4_out, not_5_out, not_6_out, not_7_out,
       not_8_out;

  not not_1 (not_1_out, S1);
  and and_1 (S11, not_1_out, S0, not_2_out);
  not not_2 (not_2_out, IN0);
  not not_3 (not_3_out, S1);
  and and_2 (and_2_out, not_3_out, not_4_out, IN0);
  not not_4 (not_4_out, IN1);
  not not_5 (not_5_out, S0);
  not not_6 (not_6_out, IN1);
  and and_3 (and_3_out, not_5_out, not_6_out, IN0);
  and and_4 (Z, S1, not_7_out, not_8_out);
  not not_7 (not_7_out, S0);
  not not_8 (not_8_out, IN0);
  or or_1 (S00, and_2_out, and_3_out);
endmodule

module \置位清零  (
  input  D,
  input  CLK,
  input  RESET,
  output Q
);

  wire multiplexer_1_out;

  Multiplexer #(.enable("false")) multiplexer_1 (.in0(D), .in1(1'b0), .out(multiplexer_1_out), .sel(RESET));
  Register #(.width(1)) register_1 (.D(multiplexer_1_out), .Q(Q), .clk(CLK));  // open: en, clr
endmodule
