// Logisim project fsm独热版.circ as structural Verilog: 4 circuits, main circuit 状态转移
module \状态转移  (
  input  S2,
  input  S1,
  input  S0,
  input  IN1,
  input  IN0,
  output S22,
  output S11,
  output S00,
  output OUT
);

  wire not_1_out, not_2_out, not_3_out, not_4_out;

  not not_1 (not_1_out, IN0);
  not not_2 (not_2_out, S1);
  not not_3 (not_3_out, IN0);
  not not_4 (not_4_out, IN0);
  and and_1 (S22, S1, not_1_out);
  and and_2 (S00, not_2_out, not_3_out);
  and and_3 (OUT, S2, not_4_out);

  assign S11 = IN0;
endmodule

module \清零  (
  input  D,
  input  CLK,
  input  RESET,
  output Q
);

  wire multiplexer_1_out;

  Register #(.width(1)) register_1 (.D(multiplexer_1_out), .Q(Q), .clk(CLK));  // open: en, clr
  Multiplexer #(.enable("false")) multiplexer_1 (.in0(D), .in1(1'b0), .out(multiplexer_1_out), .sel(RESET));
endmodule

module \输出  (
  input  reset,
  input  [1:0] in,
  output z
);

  wire CLK, S0, S00, S1, S2, S11, S22;

  Clock u_clk (.out(CLK));
  // Probe on S1
  \清零  \u_清零_1  (.D(S11), .CLK(CLK), .RESET(reset), .Q(S1));
  // Probe on S0
  \清零  \u_清零_2  (.D(S00), .CLK(CLK), .RESET(reset), .Q(S0));
  // Probe on S2
  \清零  \u_清零_3  (.D(S22), .CLK(CLK), .RESET(reset), .Q(S2));
  \状态转移  \u_状态转移_1  (.S2(S2), .S1(S1), .S0(S0), .IN1(in[1]), .IN0(in[0]), .S22(S22), .S11(S11), .S00(S00), .OUT(z));
endmodule

module fsm (
  input  in_1,
  input  [1:0] in_2,
  output out_3
);

  \输出  \u_输出_1  (.reset(in_1), .in(in_2), .z(out_3));
endmodule
