// Logisim project ftoi.circ as structural Verilog: 1 circuit, main circuit ftoi
module ftoi (
  input  [15:0] float,
  output [31:0] \int 
);

  wire comparator_1_lt, D, I_N, or_1_out;
  wire [4:0] E, subtractor_1_out;
  wire [31:0] multiplexer_1_out, multiplexer_2_out, negator_1_out, shifter_1_out, shifter_2_out,
       shifter_3_out;

  Subtractor #(.width(5)) subtractor_1 (.a(5'b01111), .b(E), .out(subtractor_1_out));  // open: bin, bout
  Comparator #(.width(5)) comparator_1 (.a(subtractor_1_out), .b({5{1'b0}}), .lt(comparator_1_lt));  // open: gt, eq
  Shifter #(.width(32)) shifter_1 (.in({22'h1, float[9:0]}), .\dist (E), .out(shifter_1_out));
  Shifter #(.width(32), .shift("lr")) shifter_2 (.in({22'h1, float[9:0]}), .\dist (E), .out(shifter_2_out));
  Subtractor #(.width(5)) subtractor_2 (.a(float[14:10]), .b(5'b01111), .out(E));  // open: bin, bout
  Multiplexer #(.width(32)) multiplexer_1 (
    .in0(shifter_1_out), .in1(shifter_2_out), .out(multiplexer_1_out), .sel(comparator_1_lt));  // open: en
  Shifter #(.width(32), .shift("lr")) shifter_3 (.in(multiplexer_1_out), .\dist (5'b01010), .out(shifter_3_out));
  Negator #(.width(32)) negator_1 (.in(shifter_3_out), .out(negator_1_out));
  Comparator #(.width(5)) comparator_2 (.a(float[14:10]), .b({5{1'b0}}), .eq(D));  // open: gt, lt
  Comparator #(.width(5)) comparator_3 (.a(float[14:10]), .b({5{1'b1}}), .eq(I_N));  // open: gt, lt
  Multiplexer #(.width(32)) multiplexer_2 (
    .in0(shifter_3_out), .in1(negator_1_out), .out(multiplexer_2_out), .sel(float[15]));  // open: en
  Multiplexer #(.width(32)) multiplexer_3 (
    .in0(multiplexer_2_out), .in1({32{1'b0}}), .out(\int ), .sel(or_1_out));  // open: en
  or or_1 (or_1_out, D, I_N);

  // Other names for the same wires on the sheet: fraction[9:0] = float[9:0]; exponent[4:0] = float[14:10];
  //   sign = float[15]
endmodule
