// Logisim project navigation.circ as structural Verilog: 2 circuits, main circuit navigation
module navigation (
  input  [1:0] dir,
  input  clk,
  input  reset,
  output arrive,
  output hit
);

  wire HIT_t, S0, S00, S1, S2, S11, S22;

  Clock u_clk ();  // open: out
  Register #(.width(1)) u_s2 (.D(S22), .Q(S2), .clk(clk), .clr(reset));  // open: en
  Register #(.width(1)) u_s1 (.D(S11), .Q(S1), .clk(clk), .clr(reset));  // open: en
  \状态转移  \u_状态转移_1  (
    .S2(S2), .S1(S1), .S0(S0), .IN1(dir[1]), .IN0(dir[0]), .S22(S22), .S11(S11), .S00(S00), .HIT(HIT_t));
  Register #(.width(1)) u_s0 (.D(S00), .Q(S0), .clk(clk), .clr(reset));  // open: en
  Register #(.width(1)) u_hit (.D(HIT_t), .Q(hit), .clk(clk), .clr(reset));  // open: en
  Register #(.width(1)) u_arrive (.D(S22), .Q(arrive), .clk(clk), .clr(reset));  // open: en

  // Other names for the same wires on the sheet: IN0 = dir[0]; IN1 = dir[1]
endmodule

module \状态转移  (
  input  S2,
  input  S1,
  input  S0,
  input  IN1,
  input  IN0,
  output S22,
  output S11,
  output S00,
  output HIT
);

  wire and_1_out, and_2_out, and_3_out, and_4_out, and_5_out, and_6_out, and_7_out, and_8_out, and_9_out,
       and_10_out, and_11_out, and_12_out, and_13_out, and_14_out, and_15_out, and_16_out, and_17_out,
       and_18_out, not_1_out, not_2_out, not_3_out, not_4_out, not_5_out, not_6_out, not_7_out, not_8_out,
       not_9_out, not_10_out, not_11_out, not_12_out, not_13_out, not_14_out, not_15_out, not_16_out,
       not_17_out, not_18_out, not_19_out, not_20_out, not_21_out, not_22_out, not_23_out, not_24_out,
       not_25_out, not_26_out, not_27_out, not_28_out, not_29_out, not_30_out, not_31_out;

  not not_1 (not_1_out, S0);
  not not_2 (not_2_out, IN1);
  not not_3 (not_3_out, IN0);
  not not_4 (not_4_out, IN1);
  not not_5 (not_5_out, S1);
  not not_6 (not_6_out, IN1);
  not not_7 (not_7_out, IN1);
  not not_8 (not_8_out, IN0);
  not not_9 (not_9_out, S0);
  not not_10 (not_10_out, IN1);
  not not_11 (not_11_out, S0);
  not not_12 (not_12_out, IN0);
  not not_13 (not_13_out, S2);
  not not_14 (not_14_out, S1);
  not not_15 (not_15_out, IN1);
  not not_16 (not_16_out, IN0);
  not not_17 (not_17_out, IN1);
  not not_18 (not_18_out, IN0);
  not not_19 (not_19_out, IN0);
  not not_20 (not_20_out, S2);
  not not_21 (not_21_out, S0);
  not not_22 (not_22_out, IN1);
  not not_23 (not_23_out, S2);
  not not_24 (not_24_out, S1);
  not not_25 (not_25_out, S0);
  not not_26 (not_26_out, S2);
  not not_27 (not_27_out, S0);
  not not_28 (not_28_out, IN0);
  not not_29 (not_29_out, S2);
  not not_30 (not_30_out, IN1);
  not not_31 (not_31_out, IN0);
  and and_1 (and_1_out, S1, not_1_out, not_2_out, not_3_out);
  and and_2 (and_2_out, S1, S0, not_4_out, IN0);
  and and_3 (and_3_out, not_5_out, S0, not_6_out);
  and and_4 (and_4_out, S0, not_7_out, not_8_out);
  and and_5 (and_5_out, S1, not_9_out, not_10_out, IN0);
  and and_6 (and_6_out, S1, not_11_out, IN1, not_12_out);
  and and_7 (and_7_out, S1, S0, IN1, IN0);
  and and_8 (and_8_out, not_13_out, not_14_out, not_15_out, not_16_out);
  and and_9 (and_9_out, S0, not_17_out, not_18_out);
  and and_10 (and_10_out, S0, IN1, IN0);
  and and_11 (and_11_out, S1, IN1, IN0);
  and and_12 (and_12_out, S1, S0, not_19_out);
  and and_13 (and_13_out, S2, S1, IN1);
  and and_14 (and_14_out, not_20_out, not_21_out, not_22_out, IN0);
  and and_15 (and_15_out, not_23_out, not_24_out, not_25_out, IN1);
  and and_16 (and_16_out, not_26_out, not_27_out, IN1, not_28_out);
  and and_17 (and_17_out, S0, IN1, IN0);
  and and_18 (and_18_out, not_29_out, S1, S0, not_30_out, not_31_out);
  or or_1 (S22, and_1_out, and_2_out);
  or or_2 (S11, and_3_out, and_4_out, and_5_out, and_6_out, and_7_out);
  or or_3 (S00, and_8_out, and_9_out, and_10_out, and_11_out, and_12_out, and_13_out);
  or or_4 (HIT, and_14_out, and_15_out, and_16_out, and_17_out, and_18_out);
endmodule
