// Logisim project CPU - 副本 - 副本.circ as structural Verilog: 8 circuits, main circuit main
module main (
  input  in_1,
  output [31:0] out_2,
  output out_3,
  output [4:0] out_4,
  output [31:0] out_5,
  output out_6,
  output [4:0] out_7,
  output [31:0] out_8
);

  wire alu_1_isodd, ALUsrc, B, CLK, JAL, JR, MemtoReg, or_1_out, or_2_out, RegDst, RegWrite, ZERO;
  wire [1:0] ExtOp, WBH;
  wire [3:0] ALUctrl;
  wire [4:0] multiplexer_2_out;
  wire [31:0] adder_1_out, alu_1_hi, alu_1_lo, ByteMemAddr, dm_1_dout, ext32, grf_1_rd1, multiplexer_1_out,
       multiplexer_5_out, multiplexer_6_out, npc_1_npc, PC;

  Clock clock_1 (.out(CLK));
  nPC npc_1 (
    .PC(PC), .OFFSET(out_2[15:0]), .instr_index(out_2[25:0]), .NPC(npc_1_npc), .op(out_2[31:26]),
    .funct(out_2[5:0]), .ZERO(ZERO), .JAL(JAL), .ISODD(alu_1_isodd), .B(B));
  Multiplexer #(.width(32), .enable("false")) multiplexer_1 (
    .in0(npc_1_npc), .in1(multiplexer_5_out), .out(multiplexer_1_out), .sel(JR));
  IFU ifu_1 (.reset(in_1), .clk(CLK), .NPC(multiplexer_1_out), .PC(PC), .Instr(out_2));
  Controller controller_1 (
    .op(out_2[31:26]), .funct(out_2[5:0]), .RegDst(RegDst), .ALUsrc(ALUsrc), .MemtoReg(MemtoReg),
    .RegWrite(RegWrite), .MemWrite(out_6), .ALUctrl(ALUctrl), .ExtOP(ExtOp), .JR(JR), .WBH(WBH));
  EXT ext_1 (.imm16(out_2[15:0]), .ext32(ext32), .ExtOp(ExtOp));
  Multiplexer #(.width(5), .enable("false")) multiplexer_2 (
    .in0(out_2[20:16]), .in1(out_2[15:11]), .out(multiplexer_2_out), .sel(RegDst));
  Multiplexer #(.width(5), .enable("false")) multiplexer_3 (
    .in0(multiplexer_2_out), .in1({5{1'b1}}), .out(out_4), .sel(or_1_out));
  or or_1 (or_1_out, JAL, B);
  or or_2 (or_2_out, B, JAL);
  GRF grf_1 (
    .WE3(out_3), .CLK(CLK), .A1(out_2[25:21]), .A2(out_2[20:16]), .in_5(in_1), .A3(out_4), .WD3(out_5),
    .RD1(grf_1_rd1), .RD2(out_8));
  Multiplexer #(.width(32), .enable("false")) multiplexer_4 (
    .in0(multiplexer_5_out), .in1(dm_1_dout), .out(out_5), .sel(MemtoReg));
  Multiplexer #(.width(32), .enable("false")) multiplexer_5 (
    .in0({ByteMemAddr[31:7], out_7, ByteMemAddr[1:0]}), .in1(adder_1_out), .out(multiplexer_5_out),
    .sel(or_2_out));
  or or_3 (out_3, RegWrite, B);
  Multiplexer #(.width(32), .enable("false")) multiplexer_6 (
    .in0(out_8), .in1(ext32), .out(multiplexer_6_out), .sel(ALUsrc));
  Adder #(.width(32)) adder_1 (.a(PC), .b(32'h4), .out(adder_1_out));  // open: cin, cout
  ALU alu_1 (
    .A(grf_1_rd1), .B(multiplexer_6_out), .offset(out_2[10:6]), .ALUctrl(ALUctrl), .out_6(ZERO),
    .C({ByteMemAddr[31:7], out_7, ByteMemAddr[1:0]}), .HI(alu_1_hi), .LO(alu_1_lo), .ISODD(alu_1_isodd));  // open: in_5
  DM dm_1 (
    .A({out_7, ByteMemAddr[1:0]}), .Din(out_8), .Dout(dm_1_dout), .MemWrite(out_6), .CLK(CLK), .RESET(in_1),
    .WBH(WBH));

  // Other names for the same wires on the sheet: ByteMemAddr[6:2] = out_7; MemAddr[4:0] = out_7;
  //   addr[25:0] = out_2[25:0]; funct[5:0] = out_2[5:0]; imm[15:0] = out_2[15:0]; Instr[31:0] = out_2;
  //   shamt[4:0] = out_2[10:6]; op[5:0] = out_2[31:26]; MemData[31:0] = out_8; MemWrite = out_6; RegAddr[4:0] = out_4;
  //   RegData[31:0] = out_5; RegWrite1 = out_3; RESET = in_1
endmodule

module GRF (
  input  WE3,
  input  CLK,
  input  [4:0] A1,
  input  [4:0] A2,
  input  in_5,
  input  [4:0] A3,
  input  [31:0] WD3,
  output [31:0] RD1,
  output [31:0] RD2
);

  wire and_1_out, and_2_out, and_3_out, and_4_out, and_5_out, and_6_out, and_7_out, and_8_out, and_9_out,
       and_10_out, and_11_out, and_12_out, and_13_out, and_14_out, and_15_out, and_16_out, and_17_out,
       and_18_out, and_19_out, and_20_out, and_21_out, and_22_out, and_23_out, and_24_out, and_25_out,
       and_26_out, and_27_out, and_28_out, and_29_out, and_30_out, and_31_out, and_32_out, WR0, WR1, WR2,
       WR3, WR4, WR5, WR6, WR7, WR8, WR9, WR10, WR11, WR12, WR13, WR14, WR15, WR16, WR17, WR18, WR19, WR20,
       WR21, WR22, WR23, WR24, WR25, WR26, WR27, WR28, WR29, WR30, WR31;
  wire [31:0] R0, R1, R2, R3, R4, R5, R6, R7, R8, R9, R10, R11, R12, R13, R14, R15, R16, R17, R18, R19, R20,
       R21, R22, R23, R24, R25, R26, R27, R28, R29, R30, R31;

  Decoder #(.select(5), .enable("false")) decoder_1 (
    .out0(WR0), .out1(WR1), .out2(WR2), .out3(WR3), .out4(WR4), .out5(WR5), .out6(WR6), .out7(WR7),
    .out8(WR8), .out9(WR9), .out10(WR10), .out11(WR11), .out12(WR12), .out13(WR13), .out14(WR14),
    .out15(WR15), .out16(WR16), .out17(WR17), .out18(WR18), .out19(WR19), .out20(WR20), .out21(WR21),
    .out22(WR22), .out23(WR23), .out24(WR24), .out25(WR25), .out26(WR26), .out27(WR27), .out28(WR28),
    .out29(WR29), .out30(WR30), .out31(WR31), .sel(A3));
  and and_1 (and_1_out, WR0, WE3);
  and and_2 (and_2_out, WR1, WE3);
  and and_3 (and_3_out, WR2, WE3);
  and and_4 (and_4_out, WR3, WE3);
  and and_5 (and_5_out, WR4, WE3);
  and and_6 (and_6_out, WR5, WE3);
  and and_7 (and_7_out, WR6, WE3);
  and and_8 (and_8_out, WR7, WE3);
  Register #(.width(32)) zero (.D({32{1'b0}}), .Q(R0), .clk(CLK), .clr(in_5));  // open: en
  Register #(.width(32)) at (.D(WD3), .en(and_2_out), .Q(R1), .clk(CLK), .clr(in_5));
  Register #(.width(32)) v0 (.D(WD3), .en(and_3_out), .Q(R2), .clk(CLK), .clr(in_5));
  Register #(.width(32)) v1 (.D(WD3), .en(and_4_out), .Q(R3), .clk(CLK), .clr(in_5));
  Register #(.width(32)) a0 (.D(WD3), .en(and_5_out), .Q(R4), .clk(CLK), .clr(in_5));
  Register #(.width(32)) u_a1 (.D(WD3), .en(and_6_out), .Q(R5), .clk(CLK), .clr(in_5));
  Register #(.width(32)) u_a2 (.D(WD3), .en(and_7_out), .Q(R6), .clk(CLK), .clr(in_5));
  Register #(.width(32)) u_a3 (.D(WD3), .en(and_8_out), .Q(R7), .clk(CLK), .clr(in_5));
  and and_9 (and_9_out, WR8, WE3);
  and and_10 (and_10_out, WR9, WE3);
  and and_11 (and_11_out, WR10, WE3);
  and and_12 (and_12_out, WR11, WE3);
  and and_13 (and_13_out, WR12, WE3);
  and and_14 (and_14_out, WR13, WE3);
  and and_15 (and_15_out, WR14, WE3);
  and and_16 (and_16_out, WR15, WE3);
  Register #(.width(32)) t0 (.D(WD3), .en(and_9_out), .Q(R8), .clk(CLK), .clr(in_5));
  Register #(.width(32)) t1 (.D(WD3), .en(and_10_out), .Q(R9), .clk(CLK), .clr(in_5));
  Register #(.width(32)) t2 (.D(WD3), .en(and_11_out), .Q(R10), .clk(CLK), .clr(in_5));
  Register #(.width(32)) t3 (.D(WD3), .en(and_12_out), .Q(R11), .clk(CLK), .clr(in_5));
  Register #(.width(32)) t4 (.D(WD3), .en(and_13_out), .Q(R12), .clk(CLK), .clr(in_5));
  Register #(.width(32)) t5 (.D(WD3), .en(and_14_out), .Q(R13), .clk(CLK), .clr(in_5));
  Register #(.width(32)) t6 (.D(WD3), .en(and_15_out), .Q(R14), .clk(CLK), .clr(in_5));
  Register #(.width(32)) t7 (.D(WD3), .en(and_16_out), .Q(R15), .clk(CLK), .clr(in_5));
  and and_17 (and_17_out, WR16, WE3);
  and and_18 (and_18_out, WR17, WE3);
  and and_19 (and_19_out, WR18, WE3);
  and and_20 (and_20_out, WR19, WE3);
  and and_21 (and_21_out, WR20, WE3);
  and and_22 (and_22_out, WR21, WE3);
  and and_23 (and_23_out, WR22, WE3);
  and and_24 (and_24_out, WR23, WE3);
  Register #(.width(32)) s0 (.D(WD3), .en(and_17_out), .Q(R16), .clk(CLK), .clr(in_5));
  Register #(.width(32)) s1 (.D(WD3), .en(and_18_out), .Q(R17), .clk(CLK), .clr(in_5));
  Register #(.width(32)) s2 (.D(WD3), .en(and_19_out), .Q(R18), .clk(CLK), .clr(in_5));
  Register #(.width(32)) s3 (.D(WD3), .en(and_20_out), .Q(R19), .clk(CLK), .clr(in_5));
  Register #(.width(32)) s4 (.D(WD3), .en(and_21_out), .Q(R20), .clk(CLK), .clr(in_5));
  Register #(.width(32)) s5 (.D(WD3), .en(and_22_out), .Q(R21), .clk(CLK), .clr(in_5));
  Register #(.width(32)) s6 (.D(WD3), .en(and_23_out), .Q(R22), .clk(CLK), .clr(in_5));
  Register #(.width(32)) s7 (.D(WD3), .en(and_24_out), .Q(R23), .clk(CLK), .clr(in_5));
  and and_25 (and_25_out, WR24, WE3);
  and and_26 (and_26_out, WR25, WE3);
  and and_27 (and_27_out, WR26, WE3);
  and and_28 (and_28_out, WR27, WE3);
  and and_29 (and_29_out, WR28, WE3);
  and and_30 (and_30_out, WR29, WE3);
  and and_31 (and_31_out, WR30, WE3);
  and and_32 (and_32_out, WR31, WE3);
  Register #(.width(32)) t8 (.D(WD3), .en(and_25_out), .Q(R24), .clk(CLK), .clr(in_5));
  Register #(.width(32)) t9 (.D(WD3), .en(and_26_out), .Q(R25), .clk(CLK), .clr(in_5));
  Register #(.width(32)) k0 (.D(WD3), .en(and_27_out), .Q(R26), .clk(CLK), .clr(in_5));
  Register #(.width(32)) k1 (.D(WD3), .en(and_28_out), .Q(R27), .clk(CLK), .clr(in_5));
  Register #(.width(32)) gp (.D(WD3), .en(and_29_out), .Q(R28), .clk(CLK), .clr(in_5));
  Register #(.width(32)) sp (.D(WD3), .en(and_30_out), .Q(R29), .clk(CLK), .clr(in_5));
  Register #(.width(32)) fp (.D(WD3), .en(and_31_out), .Q(R30), .clk(CLK), .clr(in_5));
  Register #(.width(32)) ra (.D(WD3), .en(and_32_out), .Q(R31), .clk(CLK), .clr(in_5));
  Multiplexer #(.select(5), .width(32)) multiplexer_1 (
    .in0(R0), .in1(R1), .in2(R2), .in3(R3), .in4(R4), .in5(R5), .in6(R6), .in7(R7), .in8(R8), .in9(R9),
    .in10(R10), .in11(R11), .in12(R12), .in13(R13), .in14(R14), .in15(R15), .in16(R16), .in17(R17),
    .in18(R18), .in19(R19), .in20(R20), .in21(R21), .in22(R22), .in23(R23), .in24(R24), .in25(R25),
    .in26(R26), .in27(R27), .in28(R28), .in29(R29), .in30(R30), .in31(R31), .out(RD1), .sel(A1));  // open: en
  Multiplexer #(.select(5), .width(32)) multiplexer_2 (
    .in0(R0), .in1(R1), .in2(R2), .in3(R3), .in4(R4), .in5(R5), .in6(R6), .in7(R7), .in8(R8), .in9(R9),
    .in10(R10), .in11(R11), .in12(R12), .in13(R13), .in14(R14), .in15(R15), .in16(R16), .in17(R17),
    .in18(R18), .in19(R19), .in20(R20), .in21(R21), .in22(R22), .in23(R23), .in24(R24), .in25(R25),
    .in26(R26), .in27(R27), .in28(R28), .in29(R29), .in30(R30), .in31(R31), .out(RD2), .sel(A2));  // open: en

  // Other names for the same wires on the sheet: clr = in_5
endmodule

module ALU (
  input  [31:0] A,
  input  [31:0] B,
  input  [4:0] offset,
  input  [3:0] ALUctrl,
  input  in_5,
  output out_6,
  output [31:0] C,
  output [31:0] HI,
  output [31:0] LO,
  output ISODD
);

  wire comparator_2_eq, GREATER;
  wire [4:0] bitfinder_1_index, bitfinder_2_index;
  wire [31:0] A_B, A_B_t, A_B_t_t, A_B_t_t_t, A_B_t_t_t_t, DIV_HI, DIV_LO, MUL_HI, MUL_LO, SGE, SLL, SLT,
       SRL, SRLV, SSZE, subtractor_2_out;

  Adder #(.width(32)) adder_1 (.a(A), .b(B), .out(A_B_t));  // open: cin, cout
  Subtractor #(.width(32)) subtractor_1 (.a(A), .b(B), .out(A_B_t_t));  // open: bin, bout
  Multiplier #(.width(32)) multiplier_1 (.a(A), .b(B), .out(MUL_LO), .cout(MUL_HI));  // open: cin
  Divider #(.width(32)) divider_1 (.a(A), .b(B), .out(DIV_LO), .rem(DIV_HI));  // open: upper
  Comparator #(.width(32)) comparator_1 (.a(A), .b(B), .eq(out_6));  // open: gt, lt
  not not_1 (GREATER, A_B_t_t[31]);
  Subtractor #(.width(32)) subtractor_2 (.a(A), .b(B), .out(subtractor_2_out));  // open: bin, bout
  assign A_B = A & B;  // AND_Gate and_1, 32 bits wide
  assign A_B_t_t_t_t = A | B;  // OR_Gate or_1, 32 bits wide
  assign A_B_t_t_t = A ^ B;  // XOR_Gate xor_1, 32 bits wide
  Shifter #(.width(32)) shifter_1 (.in(B), .\dist (offset), .out(SLL));
  Shifter #(.width(32), .shift("lr")) shifter_2 (.in(B), .\dist (offset), .out(SRL));
  Shifter #(.width(32), .shift("lr")) shifter_3 (.in(B), .\dist (A[4:0]), .out(SRLV));
  BitFinder #(.width(32)) bitfinder_1 (.in(A), .index(bitfinder_1_index));  // open: found
  BitFinder #(.width(32)) bitfinder_2 (.in(B), .index(bitfinder_2_index));  // open: found
  Multiplexer #(.width(32), .enable("false")) multiplexer_1 (
    .in0({32{1'b0}}), .in1(32'h1), .out(SLT), .sel(A_B_t_t[31]));
  Comparator #(.width(5)) comparator_2 (
    .a(bitfinder_1_index), .b(bitfinder_2_index), .eq(comparator_2_eq));  // open: gt, lt
  Multiplexer #(.width(32), .enable("false")) multiplexer_2 (.in0({32{1'b0}}), .in1(32'h1), .out(SGE), .sel(GREATER));
  Multiplexer #(.width(32), .enable("false")) multiplexer_3 (
    .in0(subtractor_2_out), .in1(32'h1), .out(SSZE), .sel(comparator_2_eq));
  Multiplexer #(.width(32)) multiplexer_4 (.in0(MUL_HI), .in1(DIV_HI), .out(HI), .sel(in_5));  // open: en
  Multiplexer #(.width(32)) multiplexer_5 (.in0(MUL_LO), .in1(DIV_LO), .out(LO), .sel(in_5));  // open: en
  Multiplexer #(.select(4), .width(32)) multiplexer_6 (
    .in0(A_B), .in1(A_B_t_t_t_t), .in2(A_B_t_t_t), .in3(A_B_t), .in4(A_B_t_t), .in5(MUL_LO), .in6(MUL_HI),
    .in7(DIV_LO), .in8(DIV_HI), .in9(SLL), .in10(SRL), .in11(SLT), .in12(SGE), .in13(SRLV), .in14(SSZE),
    .out(C), .sel(ALUctrl));  // open: in15, en
  xor xor_2 (ISODD, A[0], A[1], A[2], A[3], A[4], A[5], A[6], A[7], A[8], A[9], A[10], A[11], A[12], A[13], A[14], A[15], A[17], A[18], A[19], A[20], A[21], A[22], A[23], A[24], A[25], A[26], A[27], A[28], A[29], A[30], A[31], A[16]);

  // Other names for the same wires on the sheet: LESS = A_B_t_t[31]; EQUAL = out_6
endmodule

module DM (
  input  [1:0] WBH,
  input  [31:0] Din,
  input  [6:0] A,
  input  MemWrite,
  input  CLK,
  input  RESET,
  output [31:0] Dout
);

  wire [7:0] BYTE0, BYTE1, BYTE2, BYTE3, multiplexer_6_out;
  wire [15:0] multiplexer_4_out, multiplexer_5_out;
  wire [31:0] bit_extender_1_out, bit_extender_2_out, bit_extender_3_out, multiplexer_1_out,
       multiplexer_2_out, multiplexer_3_out;

  Multiplexer #(.select(2), .width(32), .enable("false")) multiplexer_1 (
    .in0({BYTE3, BYTE2, BYTE1, Din[7:0]}), .in1({BYTE3, BYTE2, Din[7:0], BYTE0}),
    .in2({BYTE3, Din[7:0], BYTE1, BYTE0}), .in3({Din[7:0], BYTE2, BYTE1, BYTE0}), .out(multiplexer_1_out),
    .sel(A[1:0]));
  Multiplexer #(.width(32), .enable("false")) multiplexer_2 (
    .in0({BYTE3, BYTE2, Din[15:0]}), .in1({Din[15:0], BYTE1, BYTE0}), .out(multiplexer_2_out), .sel(A[1]));
  Multiplexer #(.select(2), .width(32), .enable("false")) multiplexer_3 (
    .in0(Din), .in1(multiplexer_1_out), .in2(multiplexer_2_out), .out(multiplexer_3_out), .sel(WBH));  // open: in3
  Multiplexer #(.width(16), .enable("false")) multiplexer_4 (
    .in0({BYTE1, BYTE0}), .in1({BYTE3, BYTE2}), .out(multiplexer_4_out), .sel(A[1]));
  Multiplexer #(.width(16), .enable("false")) multiplexer_5 (
    .in0({BYTE1, BYTE0}), .in1({BYTE3, BYTE2}), .out(multiplexer_5_out), .sel(A[1]));
  Multiplexer #(.select(2), .width(8), .enable("false")) multiplexer_6 (
    .in0(BYTE0), .in1(BYTE1), .in2(BYTE2), .in3(BYTE3), .out(multiplexer_6_out), .sel(A[1:0]));
  RAM #(.addrWidth(5), .dataWidth(32), .bus("separate")) ram_1 (
    .addr(A[6:2]), .din(multiplexer_3_out), .data({BYTE3, BYTE2, BYTE1, BYTE0}), .str(MemWrite), .clk(CLK),
    .clr(RESET));  // open: sel, ld
  assign bit_extender_1_out = {{24{multiplexer_6_out[7]}}, multiplexer_6_out};  // Bit_Extender bit_extender_1
  assign bit_extender_2_out = {{16{multiplexer_5_out[15]}}, multiplexer_5_out};  // Bit_Extender bit_extender_2
  assign bit_extender_3_out = {{16{1'b0}}, multiplexer_4_out};  // Bit_Extender bit_extender_3
  Multiplexer #(.select(2), .width(32), .enable("false")) multiplexer_7 (
    .in0({BYTE3, BYTE2, BYTE1, BYTE0}), .in1(bit_extender_1_out), .in2(bit_extender_2_out),
    .in3(bit_extender_3_out), .out(Dout), .sel(WBH));

  // Other names for the same wires on the sheet: newBYTE[7:0] = Din[7:0]; newHALF[15:0] = Din[15:0];
  //   HALF0[15:0] = {BYTE1, BYTE0}; HALF1[15:0] = {BYTE3, BYTE2}; ByteMemAddr[1:0] = A[1:0]; HalfMemAddr = A[1]
endmodule

module EXT (
  input  [15:0] imm16,
  input  [1:0] ExtOp,
  output [31:0] ext32
);

  wire [31:0] bit_extender_1_out, bit_extender_2_out;

  assign bit_extender_1_out = {{16{1'b0}}, imm16};  // Bit_Extender bit_extender_1
  assign bit_extender_2_out = {{16{imm16[15]}}, imm16};  // Bit_Extender bit_extender_2
  Multiplexer #(.select(2), .width(32), .enable("false")) multiplexer_1 (
    .in0(bit_extender_1_out), .in1(bit_extender_2_out), .in2({imm16, {16{1'b0}}}), .out(ext32), .sel(ExtOp));  // open: in3
endmodule

module Controller (
  input  [5:0] op,
  input  [5:0] funct,
  output RegDst,
  output ALUsrc,
  output MemtoReg,
  output RegWrite,
  output MemWrite,
  output JR,
  output [1:0] WBH,
  output [1:0] ExtOP,
  output [3:0] ALUctrl
);

  wire add, addi, addu, beq, bne, j, jal, lb, lh, lhu, lui, lw, nF0, nF1, nF2, nF3, nF4, nF5, nOP0, nOP1,
       nOP2, nOP3, nOP4, nOP5, \or , ori, R, sb, sh, sll, slt, srlv, sub, subu, sw;

  and and_1 (R, nOP0, nOP1, nOP2, nOP3, nOP4, nOP5);
  and and_2 (addu, R, funct[0], nF1, nF2, nF3, nF4, funct[5]);
  and and_3 (subu, R, funct[0], funct[1], nF2, nF3, nF4, funct[5]);
  and and_4 (\or , R, funct[0], nF1, funct[2], nF3, nF4, funct[5]);
  and and_5 (sll, R, nF0, nF1, nF2, nF3, nF4, nF5);
  and and_6 (sub, R, nF0, funct[1], nF2, nF3, nF4, funct[5]);
  and and_7 (add, R, nF0, nF1, nF2, nF3, nF4, funct[5]);
  and and_8 (slt, R, nF0, funct[1], nF2, funct[3], nF4, funct[5]);
  and and_9 (JR, R, nF0, nF1, nF2, funct[3], nF4, nF5);
  and and_10 (srlv, R, nF0, funct[1], funct[2], nF3, nF4, nF5);
  not not_1 (nOP0, op[0]);
  not not_2 (nF0, funct[0]);
  not not_3 (nOP1, op[1]);
  not not_4 (nF1, funct[1]);
  and and_11 (lui, op[0], op[1], op[2], op[3], nOP4, nOP5);
  and and_12 (lb, nOP0, nOP1, nOP2, nOP3, nOP4, op[5]);
  and and_13 (sb, nOP0, nOP1, nOP2, op[3], nOP4, op[5]);
  and and_14 (lb, nOP0, nOP1, nOP2, nOP3, nOP4, op[5]);
  and and_15 (sb, nOP0, nOP1, nOP2, op[3], nOP4, op[5]);
  and and_16 (lh, op[0], nOP1, nOP2, nOP3, nOP4, op[5]);
  and and_17 (sh, op[0], nOP1, nOP2, op[3], nOP4, op[5]);
  and and_18 (lhu, op[0], nOP1, op[2], nOP3, nOP4, op[5]);
  not not_5 (nOP2, op[2]);
  not not_6 (nF2, funct[2]);
  and and_19 (ori, op[0], nOP1, op[2], op[3], nOP4, nOP5);
  and and_20 (beq, nOP0, nOP1, op[2], nOP3, nOP4, nOP5);
  and and_21 (lw, op[0], op[1], nOP2, nOP3, nOP4, op[5]);
  and and_22 (sw, op[0], op[1], nOP2, op[3], nOP4, op[5]);
  and and_23 (bne, op[0], nOP1, op[2], nOP3, nOP4, nOP5);
  and and_24 (addi, 1'b1, nOP1, nOP2, op[3], nOP4, nOP5);
  not not_7 (nOP3, op[3]);
  not not_8 (nF3, funct[3]);
  not not_9 (nOP4, op[4]);
  not not_10 (nF4, funct[4]);
  and and_25 (j, nOP0, op[1], nOP2, nOP3, nOP4, nOP5);
  and and_26 (jal, op[0], op[1], nOP2, nOP3, nOP4, nOP5);
  not not_11 (nOP5, op[5]);
  not not_12 (nF5, funct[5]);
  buf or_1 (RegDst, R);  // OR_Gate
  or or_2 (MemtoReg, lb, lhu, lw, lh);
  or or_3 (MemWrite, sh, sw, sb);
  buf or_4 (ExtOP[1], lui);  // OR_Gate
  or or_5 (ExtOP[0], lhu, lh, lw, sb, sw, addi, lb, sh);
  or or_6 (WBH[1], lh, lhu, sh);
  or or_7 (WBH[0], sb, lhu, lb);
  or or_8 (ALUctrl[3], sll, slt, srlv);
  or or_9 (ALUctrl[2], sub, bne, subu, srlv, beq);
  or or_10 (ALUsrc, lhu, sh, lui, ori, addi, sb, lw, sw, lb, lh);
  or or_11 (RegWrite, lhu, addi, ori, lui, lb, R, lw, jal, lh);
  or or_12 (ALUctrl[1], lhu, sh, lb, lui, addu, add, addi, slt, sw, lw, JR, sb, lh);
  or or_13 (ALUctrl[0], srlv, sh, lb, addu, addi, add, sll, lui, JR, ori, lw, sw, \or , slt, sb, lh, lhu);

  // Other names for the same wires on the sheet: ExtOP_0 = ExtOP[0]; ExtOP_1 = ExtOP[1]; F0 = funct[0]; F1 = funct[1];
  //   F2 = funct[2]; F3 = funct[3]; F4 = funct[4]; F5 = funct[5]; WBH_0 = WBH[0]; WBH_1 = WBH[1]
endmodule

module nPC (
  input  [31:0] PC,
  input  [5:0] op,
  input  [15:0] OFFSET,
  input  [5:0] funct,
  input  [25:0] instr_index,
  input  ZERO,
  input  ISODD,
  output [31:0] NPC,
  output JAL,
  output B
);

  wire and_8_out, and_9_out, b_t, beq_t, beqss, j_t, jr, nF0, nF1, nF2, nF3, nF4, nF5, nOP0, nOP1, nOP2,
       nOP3, nOP4, nOP5, R;
  wire [2:0] nPC_sel;
  wire [31:0] BEQ, bit_extender_1_out, J, PC_4;

  and and_1 (R, nOP0, nOP1, nOP2, nOP3, nOP4, nOP5);
  and and_2 (jr, R, nF0, nF1, nF2, funct[3], nF4, nF5);
  not not_1 (nOP0, op[0]);
  not not_2 (nF0, funct[0]);
  not not_3 (nOP1, op[1]);
  not not_4 (nF1, funct[1]);
  not not_5 (nOP2, op[2]);
  not not_6 (nF2, funct[2]);
  and and_3 (beq_t, nOP0, nOP1, op[2], nOP3, nOP4, nOP5);
  and and_4 (beqss, nOP0, nOP1, op[2], nOP3, nOP4, nOP5);
  not not_7 (nOP3, op[3]);
  not not_8 (nF3, funct[3]);
  and and_5 (b_t, nOP0, nOP1, op[2], nOP3, nOP4, nOP5);
  not not_9 (nOP4, op[4]);
  not not_10 (nF4, funct[4]);
  not not_11 (nOP5, op[5]);
  not not_12 (nF5, funct[5]);
  and and_6 (j_t, nOP0, op[1], nOP2, nOP3, nOP4, nOP5);
  and and_7 (JAL, op[0], op[1], nOP2, nOP3, nOP4, nOP5);
  and and_8 (and_8_out, beq_t, ZERO);
  and and_9 (and_9_out, beqss, ISODD);
  and and_10 (B, b_t, ZERO);
  assign bit_extender_1_out = {{14{OFFSET[15]}}, {OFFSET, 2'b00}};  // Bit_Extender bit_extender_1
  Priority_Encoder priority_encoder_1 (
    .in0(1'b1), .in1(and_8_out), .in2(j_t), .in3(JAL), .in4(and_9_out), .in5(B), .out(nPC_sel));  // open: in6, in7, en_in, gs, en_out
  Adder #(.width(32)) adder_1 (.a(PC), .b(32'h4), .out(PC_4));  // open: cin, cout
  Adder #(.width(32)) adder_2 (.a(bit_extender_1_out), .b(PC_4), .out(BEQ));  // open: cin, cout
  Subtractor #(.width(32)) subtractor_1 (
    .a({PC[31:28], instr_index, 2'b00}), .b(32'h3000), .out(J));  // open: bin, bout
  Multiplexer #(.select(3), .width(32), .enable("false")) multiplexer_1 (
    .in0(PC_4), .in1(BEQ), .in2(J), .in3(J), .in4(BEQ), .in5(BEQ), .out(NPC), .sel(nPC_sel));  // open: in6, in7

  // Other names for the same wires on the sheet: PC_31_28[3:0] = PC[31:28]; F0 = funct[0]; F1 = funct[1];
  //   F2 = funct[2]; F3 = funct[3]; F4 = funct[4]; F5 = funct[5]

  // Notes on the sheet:
  //   jr和nPC并没有关系
endmodule

module IFU (
  input  reset,
  input  clk,
  input  [31:0] NPC,
  output [31:0] PC,
  output [31:0] Instr
);

  Register #(.width(32)) u_PC (.D(NPC), .Q(PC), .clk(clk), .clr(reset));  // open: en
  ROM #(.addrWidth(24), .dataWidth(32)) rom_1 (.addr(PC[25:2]), .data(Instr));  // open: sel

  // Notes on the sheet:
  //   contents of rom_1 (hex, n*v repeats v):
  //   3c08ffff ad480004 95480006
endmodule
